# Fritzing sketch SkateDriver (saved by Fritzing 0.9.3b)
stripboards: 1

parts:
  元件1 = Arduino Uno (Rev3)
  元件2 = Bluetooth HC-05 Macho
  VCC1 = Battery

nets:
  N1: 元件1.D2, 元件2.TXD
  N2: 元件1.D4, 元件2.RXD
  GND: 元件1.GND, 元件2.GND, VCC1.-
  N3: 元件2.VCC, VCC1.+
